# Fritzing sketch meteo_ver1 (saved by Fritzing 0.8.7b)

parts:
  Součástka1 = Arduino Uno (Rev3)
  DHT1 = DHT12 Humitidy and Temperature Sensor I2C.

nets:
  N1: Součástka1.A4/SDA, DHT1.SDA
  N2: Součástka1.A5/SCL, DHT1.SCL
  3V3: Součástka1.3V3, DHT1.VDD
  GND: Součástka1.GND, DHT1.GND

notes:
  SCL
  SDA
  DHT12

custom parts:
  DHT12 Humitidy and Temperature Sensor I2C.: DHT12 Humidity and Temperature Sensor I2C. Supply voltage: 2.7V to 5.5V Current: Standby 30uA, Active 800uA Temperature: -20ºC to 60ºC, res. 0.1ºC Humidity: 20%RH to 95%RH, res. 0.1%RH ID I2C 0x5c
