# Fritzing sketch meteo_ver2 (saved by Fritzing 0.8.7b)
breadboards: 1

parts:
  Součástka1 = Arduino Uno (Rev3)
  DHT1 = DHT12 Humitidy and Temperature Sensor I2C.
  U1 = ESP8266 WiFi Module [part_number=ESP8266]

nets:
  N1: Součástka1.A4/SDA, DHT1.SDA
  N2: Součástka1.A5/SCL, DHT1.SCL
  N3: Součástka1.D0/RX, U1.TXD
  N4: Součástka1.D1/TX, U1.RXD
  3V3: Součástka1.3V3, DHT1.VDD, U1.VCC, U1.CH_PD
  GND: Součástka1.GND, DHT1.GND, U1.GND

notes:
  SCL
  SDA
  ESP8266
  DHT12

custom parts:
  DHT12 Humitidy and Temperature Sensor I2C.: DHT12 Humidity and Temperature Sensor I2C. Supply voltage: 2.7V to 5.5V Current: Standby 30uA, Active 800uA Temperature: -20ºC to 60ºC, res. 0.1ºC Humidity: 20%RH to 95%RH, res. 0.1%RH ID I2C 0x5c
  ESP8266 WiFi Module: Generic WiFi Module based on the ESP8266 with onboard PCB antenna and UART communications
